# Fritzing sketch esp32_mrfc522_fritzing (saved by Fritzing 0.9.4)
breadboards: 1

parts:
  Componente2 = RFID-RC522-v3
  U1 = ESP32S-HiLetgo [part_number=ESP32S-HiLetgo]
  S1 = Momentary Switch [package=ksa_sealed_tac_switch]
  R1 = Resistor [tolerance=±5% resistance=220 package=THT]

nets:
  N1: Componente2.SDA, U1.GPIO21
  N2: Componente2.SCK, U1.GPIO18
  N3: Componente2.MOSI, U1.GPIO23
  N4: Componente2.MISO, U1.GPIO19
  GND: Componente2.GND, U1.GND, R1.Pin_0
  N5: Componente2.RST, U1.GPIO22
  N6: Componente2.3.3V, U1.3.3
  N7: U1.VIN, S1.4
  N8: U1.GPIO4, S1.2, R1.Pin_1

notes:
  Components Used:
  - MRFC522 Board
  - ESP32 Microcontroller
  - PCB Button
  - 220 Ohm Resistor
  - Protoboard

custom parts:
  RFID-RC522-v3: A simple China made RFID-RC522 Reader (6x4 cm); do check the pin labels, as this is a MFRC522 based clone.
  ESP32S-HiLetgo: HiLetgo ESP-WROOM-32 ESP32 ESP-32S Development Board 2.4GHz Dual-Mode WiFi + Bluetooth Dual Cores Microcontroller The ESP32 integrated with Antenna switches, RF Balun, power amplifiers, low-noise amplifiers, filters, and management modules, and the entire solution occupies the least area of PCB. 2.4 GHz Wi-Fi plus Bluetooth dual-mode chip, with TSMC Ultra-low power consumption 40nm technology,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
